# Fritzing sketch example1_hybrid_sketch (saved by Fritzing 0.9.6b)
breadboards: 1

parts:
  Raspberry_Pi_Pico = Raspberry Pi Pico
  EEPROM = 28C16 [package="DIP (Dual Inline) [THT]"]
  Shift_2 = 74HC595 [package="DIP16 [THT]"]
  Shift_1 = 74HC595 [package="DIP16 [THT]"]
  Reset_Switch = Pushbutton [package="[THT]"]

nets:
  GND: Raspberry_Pi_Pico.pin_3, Raspberry_Pi_Pico.pin_8, Raspberry_Pi_Pico.pin_13, Raspberry_Pi_Pico.pin_18, Raspberry_Pi_Pico.pin_23, Raspberry_Pi_Pico.pin_28, Raspberry_Pi_Pico.pin_33, Raspberry_Pi_Pico.pin_38, EEPROM.GND, EEPROM.CE, Shift_2.GND, Shift_2.OE, Shift_1.GND, Shift_1.OE, Reset_Switch.Pin_1, Reset_Switch.Pin_2
  N1: Raspberry_Pi_Pico.pin_17, EEPROM.I/O2
  N2: Raspberry_Pi_Pico.pin_19, EEPROM.I/O1
  N3: Raspberry_Pi_Pico.pin_20, EEPROM.I/O0
  N4: Raspberry_Pi_Pico.pin_21, Shift_1.DS
  N5: Raspberry_Pi_Pico.pin_22, Shift_2.ST_CP, Shift_1.ST_CP
  N6: Raspberry_Pi_Pico.pin_24, Shift_2.SH_CP, Shift_1.SH_CP
  N7: Raspberry_Pi_Pico.pin_25, EEPROM.WE
  N8: Raspberry_Pi_Pico.pin_26, EEPROM.I/O7
  N9: Raspberry_Pi_Pico.pin_27, EEPROM.I/O6
  N10: Raspberry_Pi_Pico.pin_29, EEPROM.I/O5
  N11: Raspberry_Pi_Pico.pin_30, Reset_Switch.Pin_3, Reset_Switch.Pin_4
  N12: Raspberry_Pi_Pico.pin_31, EEPROM.I/O4
  N13: Raspberry_Pi_Pico.pin_32, EEPROM.I/O3
  VCC: Raspberry_Pi_Pico.pin_40, EEPROM.VCC, Shift_2.MR, Shift_2.VCC, Shift_1.MR, Shift_1.VCC
  N14: EEPROM.A7, Shift_1.Q7
  N15: EEPROM.A6, Shift_1.Q6
  N16: EEPROM.A5, Shift_1.Q5
  N17: EEPROM.A4, Shift_1.Q4
  N18: EEPROM.A3, Shift_1.Q3
  N19: EEPROM.A2, Shift_1.Q2
  N20: EEPROM.A1, Shift_1.Q1
  N21: EEPROM.A0, Shift_1.Q0
  N22: EEPROM.A10, Shift_2.Q2
  N23: EEPROM.OE, Shift_2.Q7
  N24: EEPROM.A9, Shift_2.Q1
  N25: EEPROM.A8, Shift_2.Q0
  N26: Shift_2.DS, Shift_1.Q7'

custom parts:
  Raspberry Pi Pico: Raspberry Pi Pico. Based around the RP2040 microcontroller the Pico is a low cost microcontroller device bringing Raspberry Pi quality, cost, and easy of use to the microcontroller space. Jan 2021, Split part in to two versions: tht (this one) and SMD. This one will drill holes for a .1 in header in pcb to allow plugging in the module as well as providing pads to solder the module to the top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
  28C16: Electrically Erasable and Programmable Read Only Memory (EEPROM) with parallel I/O. 16K memory organized as 2,048 words by 8 bits. 24 pins on a 600mil dual inline package (DIP) footprint.
