# Fritzing sketch example1_pinsOnly_sketch (saved by Fritzing 0.9.6b)
breadboards: 1

parts:
  Mod1 = Raspberry Pi Pico
  28C16_EEPROM = 28C16 [package="DIP (Dual Inline) [THT]"]
  Pico_Reset_Switch = Pushbutton [package="[THT]"]

nets:
  N1: Mod1.pin_3, Mod1.pin_8, Mod1.pin_13, Mod1.pin_18, Mod1.pin_23, Mod1.pin_28, Mod1.pin_33, Mod1.pin_38, 28C16_EEPROM.GND, 28C16_EEPROM.CE, Pico_Reset_Switch.Pin_1, Pico_Reset_Switch.Pin_2
  N2: Mod1.pin_7, 28C16_EEPROM.I/O2
  N3: Mod1.pin_9, 28C16_EEPROM.I/O1
  N4: Mod1.pin_10, 28C16_EEPROM.I/O0
  N5: Mod1.pin_11, 28C16_EEPROM.A0
  N6: Mod1.pin_12, 28C16_EEPROM.A1
  N7: Mod1.pin_14, 28C16_EEPROM.A2
  N8: Mod1.pin_15, 28C16_EEPROM.A3
  N9: Mod1.pin_16, 28C16_EEPROM.A4
  N10: Mod1.pin_17, 28C16_EEPROM.A5
  N11: Mod1.pin_19, 28C16_EEPROM.A6
  N12: Mod1.pin_20, 28C16_EEPROM.A7
  N13: Mod1.pin_21, 28C16_EEPROM.A8
  N14: Mod1.pin_22, 28C16_EEPROM.A9
  N15: Mod1.pin_24, 28C16_EEPROM.WE
  N16: Mod1.pin_25, 28C16_EEPROM.OE
  N17: Mod1.pin_26, 28C16_EEPROM.A10
  N18: Mod1.pin_27, 28C16_EEPROM.I/O7
  N19: Mod1.pin_29, 28C16_EEPROM.I/O6
  N20: Mod1.pin_30, Pico_Reset_Switch.Pin_3, Pico_Reset_Switch.Pin_4
  N21: Mod1.pin_31, 28C16_EEPROM.I/O5
  N22: Mod1.pin_32, 28C16_EEPROM.I/O4
  N23: Mod1.pin_34, 28C16_EEPROM.I/O3
  N24: Mod1.pin_40, 28C16_EEPROM.VCC

custom parts:
  Raspberry Pi Pico: Raspberry Pi Pico. Based around the RP2040 microcontroller the Pico is a low cost microcontroller device bringing Raspberry Pi quality, cost, and easy of use to the microcontroller space. Jan 2021, Split part in to two versions: tht (this one) and SMD. This one will drill holes for a .1 in header in pcb to allow plugging in the module as well as providing pads to solder the module to the top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
  28C16: Electrically Erasable and Programmable Read Only Memory (EEPROM) with parallel I/O. 16K memory organized as 2,048 words by 8 bits. 24 pins on a 600mil dual inline package (DIP) footprint.
